# Fritzing sketch breadboard_sketch_fritzing (saved by Fritzing 1.0.7)
breadboards: 1

parts:
  M1 = ESP32-C3-DevKitM-1 [part_number=ESP32-C3-DevKitM-1]
  LCD1 = 2.8" SPI TFT Module [part_number=MSP2807]
  Part1 = Thumb Joystick
  Part2 = Thumb Joystick
  SG1 = Buzzer 12mm [package=buzzer-12mm]
  R1 = Resistor [tolerance=±5% power=0.25W resistance=100 package=THT]
  R2 = Resistor [tolerance=±5% power=0.25W resistance=100 package=THT]

nets:
  GND: M1.GND-1, M1.GND-4, M1.GND-9, M1.GND-12, M1.GND-15, M1.GND-16, M1.GND-21, M1.GND-23, M1.GND-27, M1.GND-30, LCD1.pin2, Part1.GND, Part2.GND, SG1.2, R2.Pin_0
  N1: M1.19, SG1.1
  N2: M1.18, LCD1.pin4
  N3: M1.4, LCD1.pin11
  N4: M1.5, LCD1.pin13
  N5: M1.6, LCD1.pin7, LCD1.pin10
  N6: M1.7, LCD1.pin6, LCD1.pin12
  N7: M1.8, LCD1.pin14
  N8: M1.9, LCD1.pin5
  N9: M1.3V3-17, M1.3V3-18, R1.Pin_0
  N10: M1.2, Part1.VERT
  N11: M1.3, Part1.HORZ
  N12: M1.0, Part2.VERT
  N13: M1.1, Part2.HORZ
  N14: M1.10, LCD1.pin3
  N15: M1.5V-28, M1.5V-29, LCD1.pin1, LCD1.pin8
  VCC: Part1.VCC, Part2.VCC, R1.Pin_1, R2.Pin_1

custom parts:
  ESP32-C3-DevKitM-1: Espressif Esp32 DevKit v1 is one of the development board created by DOIT to evaluate the ESP-WROOM-32 module. It is based on the ESP32 microcontroller that boasts Wifi, Bluetooth, Ethernet and Low Power support all in a single chip. (vanepp) Feb 2021: converted to ESP32-C3-DevKitM-1. This chip is 30pins long (2 x15) and 11 pins width.
  2.8" SPI TFT Module: A generic 2.8 inch LCD TFT 320x240 display with touchscreen and SD card slot. Uses the ILI9341 controller, like the Adafruit displays of this size uses.
